# Fritzing sketch Circuit (saved by Fritzing 0.6.3b)
breadboards: 1

parts:
  S1 = Pushbutton [package="[THT]"]
  Arduino1 = Arduino

nets:
  N1: S1.Pin_1, S1.Pin_2, Arduino1.D2
  N2: S1.Pin_3, S1.Pin_4, Arduino1.GND
